# Fritzing sketch wiring (saved by Fritzing 0.9.3b)

parts:
  S3 = SWITCH-MOMENTARY-2 [package=reed_switch_pth]
  Windrichtungsanzeige = SWITCH-MOMENTARY-2 [package=reed_switch_pth]
  S5 = SWITCH-MOMENTARY-2 [package=reed_switch_pth]
  S6 = SWITCH-MOMENTARY-2 [package=reed_switch_pth]
  S7 = SWITCH-MOMENTARY-2 [package=reed_switch_pth]
  S8 = SWITCH-MOMENTARY-2 [package=reed_switch_pth]
  S9 = SWITCH-MOMENTARY-2 [package=reed_switch_pth]
  S10 = SWITCH-MOMENTARY-2 [package=reed_switch_pth]
  Regenmengenmesser = SWITCH-MOMENTARY-2 [package=reed_switch_pth]
  Bauteil1 = Arduino Pro Mini (3.3V)
  BME280 = BME280 Breakout
  MAX44009_/_BH1750 = BH1750
  Config-Taster = Momentary Switch [package=ksa_sealed_tac_switch]
  Anemometer = SWITCH-MOMENTARY-2 [package=reed_switch_pth]
  R4 = Resistor [tolerance=±5% resistance=3.9k package=THT]
  R5 = Resistor [tolerance=±5% resistance=8.2k package=THT]
  R6 = Resistor [tolerance=±5% resistance=120k package=THT]
  R7 = Resistor [tolerance=±5% resistance=1k package=THT]
  R8 = Resistor [tolerance=±5% resistance=2.2k package=THT]
  R9 = Resistor [tolerance=±5% resistance=64.9k package=THT]
  R10 = Resistor [tolerance=±5% resistance=82k package=THT]
  R11 = Resistor [tolerance=±5% resistance=16k package=THT]
  C4 = Ceramic Capacitor [capacitance="100 nF" package="1206 [SMD, multilayer]"]
  C5 = Ceramic Capacitor [capacitance="100 nF" package="1206 [SMD, multilayer]"]
  Antenne_~8_3cm = CC1101 [part_number=CC1101]
  part = VEML6070 [part_number=VEML6070]
  R12 = Resistor [tolerance=±5% resistance=100 package=THT]
  R13 = Resistor [tolerance=±5% resistance=100 package=THT]
  JP1 = Header 11 [package=1x11_smd_no_holes]
  Regensensor_(optional) = YL-83 Rain Sensor - Detection Board

nets:
  N1: S3.1, R6.Pin_0
  N2: Windrichtungsanzeige.1, R5.Pin_1
  GND: S5.1, Regenmengenmesser.1, Bauteil1.GND, BME280.GND, MAX44009_/_BH1750.GND, Config-Taster.4, C4.1, Antenne_~8_3cm.2, part.GND, JP1.1, JP1.2, JP1.3, JP1.5, JP1.10, Regensensor_(optional).POS
  N3: S5.2, R7.Pin_1
  N4: S6.1, R4.Pin_0
  N5: S7.1, R10.Pin_0
  N6: S8.1, R8.Pin_1
  N7: S9.2, R9.Pin_0
  N8: S10.2, R11.Pin_1
  N9: Regenmengenmesser.2, R12.Pin_1
  N10: Bauteil1.A4, BME280.SDI/SDA, MAX44009_/_BH1750.SDA, part.SDA
  N11: Bauteil1.A5, BME280.SCK/SCL, MAX44009_/_BH1750.SCL, part.SCL
  VCC: Bauteil1.VCC, BME280.3.3V, MAX44009_/_BH1750.VCC, Antenne_~8_3cm.1, part.VDD, JP1.11
  N12: Bauteil1.A2, R8.Pin_0
  N13: Bauteil1.SCK, Antenne_~8_3cm.4, JP1.9
  N14: Bauteil1.MISO, Antenne_~8_3cm.5, JP1.7
  N15: Bauteil1.MOSI, Antenne_~8_3cm.3, JP1.8
  N16: Bauteil1.D10, Antenne_~8_3cm.8
  N17: Bauteil1.D9, Regensensor_(optional).NEG
  N18: Bauteil1.D8, Config-Taster.3
  N19: Bauteil1.D7, JP1.6
  N20: Bauteil1.D5, C5.0, R13.Pin_0
  N21: Bauteil1.D3, JP1.4
  N22: Bauteil1.D2, Antenne_~8_3cm.7
  N23: Anemometer.1, C5.1
  N24: R4.Pin_1, R11.Pin_0
  N25: C4.0, R12.Pin_0

notes:
  VCC
  (z.B. 5V Netzteil)

custom parts:
  BH1750: Light Sensor
  VEML6070: This little sensor is a great way to add UV light sensing to any microcontroller project. The VEML6070 from Vishay has a true UV A light sensor and an I2C-controlled ADC that will take readings and integrate them for you over ~60ms to 500ms.
  YL-83 Rain Sensor - Detection Board: The YL-83 is a rain sensor that has more resistance when dry and less resistance when wet. The module runs at 5V.
